# Fritzing sketch pcb (saved by Fritzing 0.9.3b)
circuit board: 15.24cm x 15.24cm
breadboards: 1

parts:
  Part5 = Analog Digital MUX Breakout
  JP1 = Header 5x2 [package=avr_icsp]
  J1 = male pin header, 10 pins [form="♂ (male)"]
  J1_2 = male pin header, 10 pins [form="♂ (male)"]
  Part2 = Analog Digital MUX Breakout
  JP2 = Header 5x2 [package=avr_icsp]
  J2 = male pin header, 10 pins [form="♂ (male)"]
  J3 = male pin header, 10 pins [form="♂ (male)"]
  Part3 = Analog Digital MUX Breakout
  JP3 = Header 5x2 [package=avr_icsp]
  J4 = male pin header, 10 pins [form="♂ (male)"]
  J5 = male pin header, 10 pins [form="♂ (male)"]
  Part4 = Analog Digital MUX Breakout
  JP4 = Header 5x2 [package=avr_icsp]
  J6 = male pin header, 10 pins [form="♂ (male)"]
  J7 = male pin header, 10 pins [form="♂ (male)"]
  Pro_Micro1 = SparkFun Pro Micro
  JP5 = Header 5x2 [package=avr_icsp]

nets:
  N1: Part5.GND, JP1.1, J1.pin1, J1.pin2, J1.pin3, J1.pin4, J1.pin5, J1.pin6, J1.pin7, J1.pin8, J1.pin9, J1.pin10
  N2: Part5.VCC, JP1.2, J1_2.pin1, J1_2.pin2, J1_2.pin3, J1_2.pin4, J1_2.pin5, J1_2.pin6, J1_2.pin7, J1_2.pin8, J1_2.pin9, J1_2.pin10
  N3: Part5.S0, JP1.4
  N4: Part5.S1, JP1.6
  N5: Part5.S2, JP1.8
  N6: Part5.S3, JP1.10
  N7: Part5.SIG, JP1.3
  N8: Part2.GND, JP2.1, J2.pin1, J2.pin2, J2.pin3, J2.pin4, J2.pin5, J2.pin6, J2.pin7, J2.pin8, J2.pin9, J2.pin10
  N9: Part2.VCC, JP2.2, J3.pin1, J3.pin2, J3.pin3, J3.pin4, J3.pin5, J3.pin6, J3.pin7, J3.pin8, J3.pin9, J3.pin10
  N10: Part2.S0, JP2.4
  N11: Part2.S1, JP2.6
  N12: Part2.S2, JP2.8
  N13: Part2.S3, JP2.10
  N14: Part2.SIG, JP2.5
  N15: Part3.GND, JP3.1, J4.pin1, J4.pin2, J4.pin3, J4.pin4, J4.pin5, J4.pin6, J4.pin7, J4.pin8, J4.pin9, J4.pin10
  N16: Part3.VCC, JP3.2, J5.pin1, J5.pin2, J5.pin3, J5.pin4, J5.pin5, J5.pin6, J5.pin7, J5.pin8, J5.pin9, J5.pin10
  N17: Part3.S0, JP3.4
  N18: Part3.S1, JP3.6
  N19: Part3.S2, JP3.8
  N20: Part3.S3, JP3.10
  N21: Part3.SIG, JP3.7
  N22: Part4.GND, JP4.1, J6.pin1, J6.pin2, J6.pin3, J6.pin4, J6.pin5, J6.pin6, J6.pin7, J6.pin8, J6.pin9, J6.pin10
  N23: Part4.VCC, JP4.2, J7.pin1, J7.pin2, J7.pin3, J7.pin4, J7.pin5, J7.pin6, J7.pin7, J7.pin8, J7.pin9, J7.pin10
  N24: Part4.S0, JP4.4
  N25: Part4.S1, JP4.6
  N26: Part4.S2, JP4.8
  N27: Part4.S3, JP4.10
  N28: Part4.SIG, JP4.9
  N29: Pro_Micro1.GND, JP5.1
  N30: Pro_Micro1.10, JP5.10
  N31: Pro_Micro1.16, JP5.8
  N32: Pro_Micro1.14, JP5.6
  N33: Pro_Micro1.15, JP5.4
  N34: Pro_Micro1.A0, JP5.9
  N35: Pro_Micro1.A1, JP5.7
  N36: Pro_Micro1.A2, JP5.5
  N37: Pro_Micro1.A3, JP5.3
  N38: Pro_Micro1.VCC, JP5.2

custom parts:
  SparkFun Pro Micro: The Pro Micro is similar to the Pro Mini except with an ATmega32U4 on board. The USB transceiver inside the 32U4 allows us to add USB connectivity on-board and do away with bulky external USB interface. Based on: https://github.com/unorthodox-engineers/unorthodox-arduino/blob/master/Unorthodox/fritzing/parts/Pro%20Micro.fzpz
